# Fritzing sketch wiring (saved by Fritzing 1.0.4)
breadboards: 1

parts:
  M1 = DOIT Esp32 DevKit v1 (30 pins long, 11 pins width) [part_number=ESP32S-PIN30]
  HC-SR04_Sensor_1 = HC-SR04 Ultrasonic Distance Sensor
  LED1 = LED - 5mm [color="Red (633nm)" current=0.030A package="5 mm [THT]"]
  R1 = Resistor [tolerance=±5% power=0.25W resistance=1k package=THT]
  R2 = Resistor [tolerance=±5% resistance=2K package="0402 [SMD]"]
  R3 = Resistor [tolerance=±5% resistance=220 package="0402 [SMD]"]

nets:
  GND: M1.GND, HC-SR04_Sensor_1.GND, LED1.cathode, R2.Pin_1
  N1: M1.D34, HC-SR04_Sensor_1.ECHO, R1.Pin_1
  N2: M1.D32, HC-SR04_Sensor_1.TRIG
  N3: M1.D33, R1.Pin_0, R2.Pin_0
  N4: M1.D25, R3.Pin_1
  5V: M1.VIN, HC-SR04_Sensor_1.VCC
  N5: LED1.anode, R3.Pin_0

custom parts:
  DOIT Esp32 DevKit v1 (30 pins long, 11 pins width): The DOIT Esp32 DevKit v1 is one of the development board created by DOIT to evaluate the ESP-WROOM-32 module. It is based on the ESP32 microcontroller that boasts Wifi, Bluetooth, Ethernet and Low Power support all in a single chip. (vanepp) made breadboard work, adjusted pin numbering and labels and reduced size of schematic and cleaned up pcb. This chip is 30pins long (2 x15) and 11 pins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
